# Fritzing sketch esp_to_esp_motor_control (saved by Fritzing 1.0.2b)

parts:
  Mod1 = Heltec WiFi LoRa 32 V2 [part_number=HTIT-WB32LA]
  VCC1 = Battery block 9V
  L298N2 = L298N DC motor driver
  M1 = DC Motor [voltage_(max)=6V voltage_(min)=3V]
  M2 = DC Motor [voltage_(max)=6V voltage_(min)=3V]
  Mod2 = Heltec WiFi LoRa 32 V2 [part_number=HTIT-WB32LA]
  Part1 = Thumb Joystick
  VCC2 = Battery block 9V

nets:
  N1: Mod1.pin_4, L298N2.ENA
  N2: Mod1.pin_5, L298N2.IN1
  N3: Mod1.pin_6, L298N2.IN2
  GND: Mod1.GND, VCC1.-, L298N2.GND
  N4: Mod1.pin_20, L298N2.5V
  N5: Mod1.pin_35, L298N2.IN4
  N6: Mod1.pin_36, L298N2.IN3
  N7: VCC1.+, L298N2.12V
  N8: L298N2.OUT1, M1.pin_2
  N9: L298N2.OUT2, M1.pin_1
  N10: L298N2.OUT3, M2.pin_1
  N11: L298N2.OUT4, M2.pin_2
  GND_2: Mod2.GND, Part1.GND, VCC2.-
  N12: Mod2.pin_20, Part1.VCC, VCC2.+
  N13: Mod2.pin_32, Part1.HORZ
  N14: Mod2.pin_33, Part1.VERT

custom parts:
  L298N DC motor driver: 2x DC motor driver with 78M05 positive voltage regulator (7..35 V) L298N: max 46 V, 2 A Set 5 V Enable jumper to enable 5 V regultor (needed for the L298N) and +5 V output at screw terminal or supply external +5 V at screw terminal Set ENA and/or ENB to +5 V to enable motor permanently or supply ENA and/or ENB with PWM signal IN1 and IN2 set rotation directory for motor A (OUT1/OUT2) IN2 and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
